# Fritzing sketch Cicuit (saved by Fritzing 0.9.3b)
breadboards: 1

parts:
  RTC_DS3231 = ZS-042 RTC Module
  Arduino_UNO = Arduino Uno (Rev3)
  Ethernet_shield_ver_2 = Arduino Ethernet Shield (Rev3)
  KPE_110_piezo = Piezo Speaker
  Thermistor_1kOhm = Temperature Sensor (Thermistor) [thermistor_type=NTC package=THT]
  Resistor_1kOhm = Resistor [tolerance=±5% resistance=220 package="0603 [SMD]"]  # not connected
  Maybe_use_better_version_named_SHT75 = SHT1x-Breakout

nets:
  GND: RTC_DS3231.GND, Arduino_UNO.GND, Ethernet_shield_ver_2.GND, Maybe_use_better_version_named_SHT75.GND
  5V: RTC_DS3231.VCC, Arduino_UNO.5V, Ethernet_shield_ver_2.5V, KPE_110_piezo.pin1, Thermistor_1kOhm.pin_0
  N1: RTC_DS3231.SDA, Arduino_UNO.A4/SDA, Ethernet_shield_ver_2.A4/SDA
  N2: RTC_DS3231.SCL, Arduino_UNO.A5/SCL, Ethernet_shield_ver_2.A5/SCL
  N3: Arduino_UNO.A0, Ethernet_shield_ver_2.A0, Thermistor_1kOhm.pin_1
  N4: Arduino_UNO.A1, Ethernet_shield_ver_2.A1
  N5: Arduino_UNO.A2, Ethernet_shield_ver_2.A2
  N6: Arduino_UNO.A3, Ethernet_shield_ver_2.A3
  N7: Arduino_UNO.D8, Ethernet_shield_ver_2.D8, KPE_110_piezo.pin2
  N8: Arduino_UNO.D9_PWM, Ethernet_shield_ver_2.PWM_D9
  N9: Arduino_UNO.D10_PWM/SS, Ethernet_shield_ver_2.ETH_CS
  N10: Arduino_UNO.D11_PWM/MOSI, Ethernet_shield_ver_2.PWM_D11
  N11: Arduino_UNO.D12/MISO, Ethernet_shield_ver_2.SPI/D12
  N12: Arduino_UNO.D13/SCK, Ethernet_shield_ver_2.SPI/D13
  N13: Arduino_UNO.AREF, Ethernet_shield_ver_2.AREF
  N14: Arduino_UNO.D0/RX, Ethernet_shield_ver_2.RX/D0
  N15: Arduino_UNO.D1/TX, Ethernet_shield_ver_2.TX/D1
  N16: Arduino_UNO.D2, Ethernet_shield_ver_2.D2, Maybe_use_better_version_named_SHT75.DATA
  N17: Arduino_UNO.D3_PWM, Ethernet_shield_ver_2.PWM_D3, Maybe_use_better_version_named_SHT75.SCK
  N18: Arduino_UNO.D4, Ethernet_shield_ver_2.SDCS
  N19: Arduino_UNO.D5_PWM, Ethernet_shield_ver_2.PWM_D5
  N20: Arduino_UNO.D6_PWM, Ethernet_shield_ver_2.PWM_D6
  N21: Arduino_UNO.D7, Ethernet_shield_ver_2.D7
  N22: Arduino_UNO.ioref, Ethernet_shield_ver_2.IOREF
  N23: Arduino_UNO.RESET, Ethernet_shield_ver_2.RESET
  3V3: Arduino_UNO.3V3, Ethernet_shield_ver_2.3V3, Maybe_use_better_version_named_SHT75.VCC
  VIN: Arduino_UNO.VIN, Ethernet_shield_ver_2.VIN
  N24: Arduino_UNO.N/C, Ethernet_shield_ver_2.N/A
